# Fritzing sketch i2c_ex (saved by Fritzing 0.9.6b)
breadboards: 2

parts:
  J1 = shrouded pin header, 12 pins [form="♂ (shrouded male)"]
  Part1 = Adafruit TSL2561 [part_number="Adafruit #439"]
  Part3 = BME280 Breakout

nets:
  N1: J1.pin3, Part1.SCL, Part3.SCK/SCL
  N2: J1.pin4, Part1.SDA, Part3.SDI/SDA
  GND: J1.pin5, Part1.GND, Part3.GND, Part3.SDO/ADR
  VIN: J1.pin6, Part1.VIN, Part3.3.3V

notes:
  Devkit/PMOD1
  I2C_CLK -> IO40
  I2C_DAT -> IO41
  BME280/SDO -> GND

custom parts:
  Adafruit TSL2561: The TSL2561 luminosity sensor is an advanced digital light sensor, ideal for use in a wide range of light situations. Compared to low cost CdS cells, this sensor is more precise, allowing for exact lux calculations and can be configured for different gain/timing ranges to detect light ranges from up to 0.1 - 40,000+ Lux on the fly. The best part of this sensor is that it contains both infrared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
