# Fritzing sketch flatbuffers_ex (saved by Fritzing 0.9.6b)

parts:
  J1 = shrouded pin header, 12 pins [form="♂ (shrouded male)"]
  R1 = Photocell (LDR) [package=THT]
  R2 = Resistor [tolerance=±5% resistance=10000 package="0402 [SMD]"]
  J2 = shrouded pin header, 12 pins [form="♂ (shrouded male)"]

nets:
  N1: J1.pin12, R1.pin_0, R2.Pin_0
  N2: R1.pin_1, J2.pin7
  N3: R2.Pin_1, J2.pin8

notes:
  PMOD2
  G9 -> LDR
  PMOD1
  Pull-up -> 3.3V
  Gnd -> LDR
